# Fritzing sketch tugas1 (saved by Fritzing 0.9.3b)
breadboards: 1

parts:
  Part1 = Arduino Uno (Rev3)
  LED1 = LED - 5mm [color="Red (633nm)" package="5 mm [THT]"]
  R1 = Resistor [tolerance=±5% resistance=220 package=THT]
  R2 = Resistor [tolerance=±5% resistance=220 package=THT]
  R3 = Resistor [tolerance=±5% resistance=220 package=THT]  # not connected
  C1 = Ceramic Capacitor [capacitance=100nF package="100 mil [THT, multilayer]"]
  MIC1 = Microphone
  R4 = Resistor [tolerance=±5% resistance=220 package=THT]

nets:
  N1: Part1.A2, R1.Pin_1, C1.1
  N2: Part1.D2, LED1.anode
  N3: Part1.GND, R1.Pin_0, MIC1.pin1, R4.Pin_0
  N4: LED1.cathode, R4.Pin_1
  N5: R2.Pin_1, C1.0, MIC1.pin2

// code stored in the sketch: tugas1.ino
Serial.begin(9600);   
Serial.begin(9600);           
  pinMode(2, OUTPUT);       
}

void loop() {
  int analog_val;                
  static bool led_state = false; 
  
  analog_val = analogRead(A2);

  if (analog_val > 10) {      
   
    if (led_state) {
      led_state = false;    
      digitalWrite(2, LOW);
      Serial.println(analog_val); 
    }
    else {
      led_state = true;
      digitalWrite(2, HIGH);
      Serial.println(analog_val);
    }
    delay(50);
  }
}
